# Fritzing sketch esusbarduino (saved by Fritzing 1.0.4)
breadboards: 1

parts:
  ARDUINO_UNO = Arduino Uno (Rev3)
  R1 = Resistor [tolerance=±5% power=0.25W resistance=2200 package=THT]
  R3 = Resistor [tolerance=±5% power=0.25W resistance=1000 package=THT]
  ESP01 = ESP8266 ESP-01 Upgraded WiFi Module [part_number=ESP8266]

nets:
  N1: ARDUINO_UNO.D0/RX, R3.Pin_0
  N2: ARDUINO_UNO.D1/TX, ESP01.TXD
  GND: ARDUINO_UNO.RESET, ARDUINO_UNO.GND, R1.Pin_1, ESP01.GND
  3V3: ARDUINO_UNO.3V3, ESP01.VCC, ESP01.GPIO_0, ESP01.CH_PD
  N3: R1.Pin_0, R3.Pin_1, ESP01.RXD

notes:
  O reset continuo é necessário devido que o microcontrolador vai querer continuar se comunicando com o converosor USB-SERIAL, isso "desliga" o chip principal e deixa a UART livre
  O chip do Arduino trabalha com 5V, o ESP01 com 3.3V na UART, uma forma simples de mapear isso é um divisor de tensão 1k-2.2k no RX ESP01, contudo o TX do ESP não enviará dados em 5V impossibilitando esse caminho, um conversor de nível lógico resolve, o único ponto negativo pelo que vi é que o monitor serial não funciona bem ou não funciona

custom parts:
  ESP8266 ESP-01 Upgraded WiFi Module: Upgraded Version ESP-01,all Flash are upgraded to 1M byte.Also support Cloud service remote transmission.
